# Fritzing sketch Final Circuit Diagram (saved by Fritzing 0.9.1b)
breadboards: 1

parts:
  Part1 = Arduino Uno (Rev3)
  U1 = POT_SWITCH [package=pot_pth]
  J1 = Piezo Speaker
  R1 = Resistor [tolerance=±5% resistance=1k package=THT]
  Q1 = NPN-Transistor [package="TO92 [THT]"]
  M1 = DC Motor
  VCC1 = 4 x AAA Battery Mount
  LED1 = LED - 5mm [color="Red (633nm)" package="5 mm [THT]"]
  LED2 = LED - 5mm [color="Green (555nm)" package="5 mm [THT]"]

nets:
  N1: Part1.A0, J1.pin2, R1.Pin_1
  N2: Part1.A4/SDA, U1.G$1_A
  N3: Part1.GND, U1.G$1_E, J1.pin1, R1.Pin_0, M1.pin_1, VCC1.-, LED1.cathode, LED2.cathode
  N4: Part1.D5_PWM, Q1.B
  N5: Part1.D6_PWM, LED1.anode
  N6: Part1.D7, LED2.anode
  N7: Part1.5V, U1.G$2_1
  N8: Q1.E, M1.pin_2
  N9: Q1.C, VCC1.+
